// Logisim project ControlUnitC.circ as structural Verilog: 4 circuits, main circuit ControlUnit
module ControlUnit (
  input  [4:0] Opcode,
  input  [1:0] Function,
  output [3:0] ALUop,
  output ALUSrc,
  output signExtend,
  output RegWrite,
  output [1:0] RegDest,
  output [1:0] RegWSrc,
  output memoryRead,
  output memoryWrite,
  output [1:0] PCSrc,
  output [1:0] BrachOP,
  output JumpOP
);

  ALUControlUnit alucontrolunit_1 (
    .OP0(Opcode[0]), .OP1(Opcode[1]), .OP2(Opcode[2]), .OP3(Opcode[3]), .OP4(Opcode[4]), .F0(Function[0]),
    .F1(Function[1]), .ALUop0(ALUop[0]), .ALUop1(ALUop[1]), .ALUop2(ALUop[2]), .ALUop3(ALUop[3]),
    .ALUSrc(ALUSrc), .signExtend(signExtend));
  RegistersMemoryControlUnit registersmemorycontrolunit_1 (
    .OP0(Opcode[0]), .OP1(Opcode[1]), .OP2(Opcode[2]), .OP3(Opcode[3]), .OP4(Opcode[4]), .F0(Function[0]),
    .F1(Function[1]), .RegWrite(RegWrite), .RegDest0(RegDest[0]), .RegDest1(RegDest[1]),
    .RegWSrc0(RegWSrc[0]), .RegWSrc1(RegWSrc[1]), .memoryRead(memoryRead), .memoryWrite(memoryWrite));
  ProgramCounterControlUnit programcountercontrolunit_1 (
    .OP0(Opcode[0]), .OP1(Opcode[1]), .OP2(Opcode[2]), .OP3(Opcode[3]), .OP4(Opcode[4]), .F0(Function[0]),
    .F1(Function[1]), .PCSrc0(PCSrc[0]), .PCSrc1(PCSrc[1]), .BrachOP0(BrachOP[0]), .BranchOP1(BrachOP[1]),
    .JumpOP(JumpOP));
endmodule

module ALUControlUnit (
  input  OP0,
  input  OP1,
  input  OP2,
  input  OP3,
  input  OP4,
  input  F0,
  input  F1,
  output ALUop0,
  output ALUop1,
  output ALUop2,
  output ALUop3,
  output ALUSrc,
  output signExtend
);
endmodule

module RegistersMemoryControlUnit (
  input  OP0,
  input  OP1,
  input  OP2,
  input  OP3,
  input  OP4,
  input  F0,
  input  F1,
  output RegWrite,
  output RegDest0,
  output RegDest1,
  output RegWSrc0,
  output RegWSrc1,
  output memoryRead,
  output memoryWrite
);
endmodule

module ProgramCounterControlUnit (
  input  OP0,
  input  OP1,
  input  OP2,
  input  OP3,
  input  OP4,
  input  F0,
  input  F1,
  output PCSrc0,
  output PCSrc1,
  output BrachOP0,
  output BranchOP1,
  output JumpOP
);
endmodule
