// Logisim project JBControl.circ as structural Verilog
module JumpControl (
  input  [15:0] PC,
  input  [15:0] Rs,
  input  [10:0] Imm1,
  input  JOperation,
  output [15:0] newPC
);

  wire [15:0] adder_1_out, Imm;

  assign Imm = {{5{Imm1[10]}}, Imm1};  // Bit_Extender bit_extender_1
  Adder #(.width(16)) adder_1 (.a(PC), .b(Imm), .out(adder_1_out), .cin(1'b0));  // open: cout
  Multiplexer #(.width(16), .enable("false")) multiplexer_1 (
    .in0(adder_1_out), .in1(Rs), .sel(JOperation));  // open: out
endmodule
