// Logisim project RegisterFileC.circ as structural Verilog: 1 circuit, main circuit RegisterFile
module RegisterFile (
  input  Reg_Write,
  input  CLK,
  input  [2:0] RA,
  input  [2:0] RB,
  input  [2:0] RW,
  input  [15:0] Bus_W,
  output [15:0] Bus_A,
  output [15:0] Bus_B,
  output [15:0] R1,
  output [15:0] R4,
  output [15:0] R7,
  output [15:0] R2,
  output [15:0] R5,
  output [15:0] R3,
  output [15:0] R6
);

  wire S1, S2, S3, S4, S5, S6, S7;

  Decoder #(.select(3), .enable("false")) decoder_1 (
    .out1(S1), .out2(S2), .out3(S3), .out4(S4), .out5(S5), .out6(S6), .out7(S7), .sel(RW));  // open: out0
  // FRU fru_1: pin names not known; wires that end beside it: S1, Reg_Write, Bus_W, R1, CLK
  // FRU fru_2: pin names not known; wires that end beside it: S5, Reg_Write, Bus_W, R5, CLK
  // FRU fru_3: pin names not known; wires that end beside it: S2, Reg_Write, Bus_W, R2, CLK
  // FRU fru_4: pin names not known; wires that end beside it: S6, Reg_Write, Bus_W, R6, CLK
  RegisterSelector registerselector_1 (
    .Register_S(RA), .R1(R1), .R2(R2), .R3(R3), .R4(R4), .R5(R5), .R6(R6), .R7(R7), .out_9(Bus_A));
  // FRU fru_5: pin names not known; wires that end beside it: S3, Reg_Write, Bus_W, R3, CLK
  // FRU fru_6: pin names not known; wires that end beside it: S7, Reg_Write, Bus_W, R7, CLK
  RegisterSelector registerselector_2 (
    .Register_S(RB), .R1(R1), .R2(R2), .R3(R3), .R4(R4), .R5(R5), .R6(R6), .R7(R7), .out_9(Bus_B));
  // FRU fru_7: pin names not known; wires that end beside it: S4, Reg_Write, Bus_W, R4, CLK
endmodule
